# Fritzing sketch Main Schematic (saved by Fritzing 1.0.4)
breadboards: 2

parts:
  U1 = ESP32S-HiLetgo [part_number=ESP32S-HiLetgo]
  U2 = ESP32S-HiLetgo [part_number=ESP32S-HiLetgo]
  Power_plug1 = Power plug
  J11 = Basic Servo
  J12 = Basic Servo
  J14 = Basic Servo
  J13 = Basic Servo
  J5 = Basic Servo
  J10 = Basic Servo
  J8 = Basic Servo
  J15 = Basic Servo
  J16 = Basic Servo
  J17 = Basic Servo
  J18 = Basic Servo
  J19 = Basic Servo
  J20 = Basic Servo
  J21 = Basic Servo
  J22 = Basic Servo
  J23 = Basic Servo
  J24 = Basic Servo
  J25 = Basic Servo
  J26 = Basic Servo
  J27 = Basic Servo
  J28 = Basic Servo
  J29 = Basic Servo
  J30 = Basic Servo
  J31 = Basic Servo
  U3 = WS2812 RGB LED strip
  M1 = RioRand LM2596
  M2 = RioRand LM2596
  M3 = RioRand LM2596
  M4 = RioRand LM2596
  M5 = RioRand LM2596
  M6 = RioRand LM2596

nets:
  N1: U1.GPIO35, J24.pulse
  N2: U1.GPIO32, J25.pulse
  N3: U1.GPIO33, J26.pulse
  N4: U1.GPIO25, J28.pulse
  N5: U1.GPIO26, J29.pulse
  N6: U1.GPIO27, J30.pulse
  N7: U1.GPIO14, J27.pulse
  N8: U1.GPIO12, J31.pulse
  GND: U1.GND, U2.GND, Power_plug1.GND, J13.pulse, U3.GND, U3.DIN, M1.Pin_1, M2.Pin_1, M3.Pin_1, M4.Pin_1
  VIN: U1.VIN, U2.VIN
  N9: U1.GPIO15, J5.pulse
  N10: U1.GPIO2, J8.pulse
  N11: U1.GPIO4, J10.pulse
  N12: U1.GPIO16, U2.GPIO1
  N13: U1.GPIO17, U2.GPIO3
  N14: U1.GPIO5, J11.pulse
  N15: U1.GPIO18, J12.pulse
  N16: U1.GPIO19, J14.pulse
  N17: U1.GPIO3, J15.pulse
  N18: U2.GPIO35, J23.pulse
  N19: U2.GPIO32, J19.pulse
  N20: U2.GPIO33, J22.pulse
  N21: U2.GPIO25, J21.pulse
  N22: U2.GPIO26, J20.pulse
  N23: U2.GPIO27, J18.pulse
  N24: U2.GPIO14, J17.pulse
  N25: U2.GPIO12, J16.pulse
  VCC: Power_plug1.VCC, U3.VCC, M1.Pin_2, M2.Pin_2, M3.Pin_2, M4.Pin_2, M5.Pin_2, M6.Pin_2
  N26: J12.vcc, M1.Pin_3, M2.Pin_3
  N27: J5.gnd, M1.Pin_4
  N28: J8.gnd, M2.Pin_4
  N29: J16.gnd, M6.Pin_4
  N30: J17.gnd, M5.Pin_4
  N31: J21.vcc, M6.Pin_3
  N32: J24.gnd, M4.Pin_4
  N33: J25.gnd, M3.Pin_4
  N34: J29.vcc, M4.Pin_3
  N35: M5.Pin_1, M6.Pin_1

custom parts:
  ESP32S-HiLetgo: HiLetgo ESP-WROOM-32 ESP32 ESP-32S Development Board 2.4GHz Dual-Mode WiFi + Bluetooth Dual Cores Microcontroller The ESP32 integrated with Antenna switches, RF Balun, power amplifiers, low-noise amplifiers, filters, and management modules, and the entire solution occupies the least area of PCB. 2.4 GHz Wi-Fi plus Bluetooth dual-mode chip, with TSMC Ultra-low power consumption 40nm technology,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
  WS2812 RGB LED strip: WS2812 strip
